// Logisim project circuitos.circ as structural Verilog: 8 circuits, main circuit main
module main (
);

  validador validador_1 ();  // open: IN_01, in_3, WRITE__W, DUPLICATE__D, OUT_01, out_6
  enrutador_7_a_9 enrutador_7_a_9_1 ();  // open: _0, _1, _2, _3, _4, _5, _6, _7, _0_2, _1_2, _2_2, _3_2, _4_2, _5_2, _6_2, out_16, _7_2, out_18, _8, out_20, _9, out_22

  // Notes on the sheet:
  //   COORDINATOR
endmodule

module toggle (
  input  in_1,
  output out_2
);

  wire d_ff_1_q, not_1_out, xor_1_out;

  D_Flip_Flop #(.NewFFLayout("false")) d_ff_1 (.clk(xor_1_out), .D(1'b1), .Q(d_ff_1_q));  // open: Qn, preset, reset
  xor xor_1 (xor_1_out, in_1, d_ff_1_q);
  not not_1 (not_1_out, xor_1_out);
  T_Flip_Flop #(.NewFFLayout("false")) t_ff_1 (.clk(not_1_out), .T(1'b1), .Q(out_2));  // open: Qn, preset, reset
endmodule

module semaforo_transito (
  input  [1:0] in_1,
  output out_2,
  output out_3,
  output out_4
);

  wire nor_1_out, nor_4_out, not_1_out, not_2_out, not_3_out;

  not not_1 (not_1_out, in_1[1]);
  nor nor_1 (nor_1_out, not_1_out, out_4);
  nor nor_2 (out_4, in_1[1], nor_1_out);
  not not_2 (not_2_out, in_1[0]);
  nor nor_3 (out_2, not_2_out, nor_4_out);
  nor nor_4 (nor_4_out, in_1[0], out_2);
  not not_3 (not_3_out, out_4);
  and and_1 (out_3, nor_4_out, not_3_out);
endmodule

module validador (
  input  WRITE__W,
  input  IN_01,
  input  in_3,
  output DUPLICATE__D,
  output OUT_01,
  output out_6
);

  wire and_1_out, and_2_out, Retraso_out_2;

  comparador_2_bits Comparador (.in_1(IN_01), .in_3(in_3), .out_5(DUPLICATE__D), .in_2(OUT_01), .in_4(out_6));
  and and_1 (and_1_out, WRITE__W, IN_01);
  and and_2 (and_2_out, WRITE__W, in_3);
  retraso Retraso (.in_1(WRITE__W), .out_2(Retraso_out_2));
  memoria_2_bits Memoria (.in_1(and_1_out), .in_2(and_2_out), .in_3(Retraso_out_2), .out_4(OUT_01), .out_5(out_6));

  // Notes on the sheet:
  //   $$$$$
endmodule

module retraso (
  input  in_1,
  output out_2
);

  wire not_1_out;

  not not_1 (not_1_out, in_1);
  not not_2 (out_2, not_1_out);
endmodule

module memoria_2_bits (
  input  in_1,
  input  in_2,
  input  in_3,
  output out_4,
  output out_5
);

  D_Flip_Flop #(.NewFFLayout("false")) d_ff_1 (.clk(in_3), .D(in_1), .Q(out_4));  // open: Qn, preset, reset
  D_Flip_Flop #(.NewFFLayout("false")) d_ff_2 (.clk(in_3), .D(in_2), .Q(out_5));  // open: Qn, preset, reset
endmodule

module comparador_2_bits (
  input  in_1,
  input  in_2,
  input  in_3,
  input  in_4,
  output out_5
);

  wire xnor_1_out, xnor_2_out;

  xnor xnor_1 (xnor_1_out, in_1, in_2);
  and and_1 (out_5, xnor_1_out, xnor_2_out);
  xnor xnor_2 (xnor_2_out, in_3, in_4);
endmodule

module enrutador_7_a_9 (
  input  _0,
  input  _1,
  input  _2,
  input  _3,
  input  _4,
  input  _5,
  input  _6,
  input  _7,
  output _0_2,
  output _1_2,
  output _2_2,
  output _3_2,
  output _4_2,
  output _5_2,
  output _6_2,
  output out_16,
  output _7_2,
  output out_18,
  output _8,
  output out_20,
  output _9,
  output out_22
);

  or or_1 (_0_2, _0, _5);
  or or_2 (_2_2, _1, _6);
  or or_3 (_3_2, _2, _7);
  or or_4 (_5_2, _3, _4);

  assign _1_2 = _0;
  assign _4_2 = _2;
  assign _6_2 = _4;
  assign _7_2 = _5;
  assign _8 = _6;
  assign _9 = _7;
  assign out_16 = _4;
  assign out_18 = _5;
  assign out_20 = _6;
  assign out_22 = _7;

  // Notes on the sheet:
  //   Fases
  //   Semáforos
endmodule
